// Logisim project mips-single.circ as structural Verilog: 6 circuits, main circuit main
// ALU
module main (
  input  in_1
);

  wire alucontrol_1_jrdetect, and_1_out, clock_1_out, comparator_1_eq, comparator_2_lt, comparator_3_lt,
       comparator_4_eq, multiplexer_9_out, not_1_out, not_2_out;
  wire [3:0] mips_alu_1_p3;
  wire [4:0] multiplexer_4_out, multiplexer_5_out, multiplexer_6_out;
  wire [11:0] rom_1_data;
  wire [31:0] adder_1_out, adder_2_out, bit_extender_1_out, bit_extender_2_out, memory_1_out_7,
       mips_alu_1_p5, mipsprogramrom_1_p2, multiplexer_1_out, multiplexer_2_out, multiplexer_3_out,
       multiplexer_7_out, multiplexer_8_out, multiplexer_10_out, multiplexer_11_out, register_1_q,
       registerfile_1_p1, registerfile_1_p7, registerfile_1_p8, shifter_1_out, shifter_2_out,
       sign_extend_1_out_2;

  Multiplexer #(.width(32), .enable("false")) multiplexer_1 (
    .in0(multiplexer_3_out), .in1(registerfile_1_p7), .out(multiplexer_1_out), .sel(alucontrol_1_jrdetect));
  Clock clock_1 (.out(clock_1_out));
  Multiplexer #(.width(32), .enable("false")) multiplexer_2 (
    .in0(adder_2_out), .in1(adder_1_out), .out(multiplexer_2_out), .sel(and_1_out));
  Adder #(.width(32)) adder_1 (.a(adder_2_out), .b(shifter_2_out), .out(adder_1_out));  // open: cin, cout
  assign bit_extender_1_out = {{6{mipsprogramrom_1_p2[25]}}, mipsprogramrom_1_p2[25:0]};  // Bit_Extender bit_extender_1
  Shifter #(.width(32)) shifter_1 (.in(bit_extender_1_out), .\dist (5'b00010), .out(shifter_1_out));
  Register #(.width(32)) register_1 (
    .D(multiplexer_1_out), .clk(clock_1_out), .Q(register_1_q), .clr(in_1));  // open: en
  Adder #(.width(32)) adder_2 (.a(register_1_q), .b(32'h4), .out(adder_2_out));  // open: cin, cout
  Multiplexer #(.width(32), .enable("false")) multiplexer_3 (
    .in0(multiplexer_2_out), .in1(shifter_1_out), .out(multiplexer_3_out), .sel(rom_1_data[0]));
  // MIPSProgramROM mipsprogramrom_1: pin names not known; wires that end beside it: register_1_q, mipsprogramrom_1_p2
  Shifter #(.width(32)) shifter_2 (.in(sign_extend_1_out_2), .\dist (5'b00010), .out(shifter_2_out));
  Multiplexer #(.width(5), .enable("false")) multiplexer_4 (
    .in0(mipsprogramrom_1_p2[25:21]), .in1({5{1'b1}}), .out(multiplexer_4_out), .sel(alucontrol_1_jrdetect));
  ROM #(.addrWidth(6), .dataWidth(12)) rom_1 (.addr(mipsprogramrom_1_p2[31:26]), .data(rom_1_data));
  Multiplexer #(.width(5), .enable("false")) multiplexer_5 (
    .in0(mipsprogramrom_1_p2[20:16]), .in1(mipsprogramrom_1_p2[15:11]), .out(multiplexer_5_out),
    .sel(rom_1_data[7]));
  Sign_Extend sign_extend_1 (.in_1(mipsprogramrom_1_p2), .out_2(sign_extend_1_out_2));
  and and_1 (and_1_out, mips_alu_1_p5[0], rom_1_data[1]);
  Multiplexer #(.width(5), .enable("false")) multiplexer_6 (
    .in0(multiplexer_5_out), .in1({5{1'b1}}), .out(multiplexer_6_out), .sel(rom_1_data[0]));
  // RegisterFile registerfile_1: pin names not known; wires that end beside it: registerfile_1_p1, clock_1_out, rom_1_data[4], multiplexer_6_out, multiplexer_4_out, mipsprogramrom_1_p2[20:16], registerfile_1_p7, registerfile_1_p8
  Multiplexer #(.width(32), .enable("false")) multiplexer_7 (
    .in0(registerfile_1_p8), .in1(sign_extend_1_out_2), .out(multiplexer_7_out), .sel(rom_1_data[6]));
  Multiplexer #(.width(32), .enable("false")) multiplexer_8 (
    .in0(registerfile_1_p8), .in1(sign_extend_1_out_2), .out(multiplexer_8_out), .sel(not_1_out));
  not not_1 (not_1_out, comparator_1_eq);
  Comparator #(.width(6)) comparator_1 (
    .a({6{1'b0}}), .b(mipsprogramrom_1_p2[31:26]), .eq(comparator_1_eq));  // open: gt, lt
  // Mips_ALU mips_alu_1: pin names not known; wires that end beside it: registerfile_1_p7, multiplexer_7_out, mips_alu_1_p3, mipsprogramrom_1_p2[10:6], mips_alu_1_p5
  Comparator #(.width(32)) comparator_2 (
    .a(registerfile_1_p7), .b(multiplexer_8_out), .lt(comparator_2_lt));  // open: gt, eq
  Comparator #(.width(32), .mode("unsigned")) comparator_3 (
    .a(registerfile_1_p7), .b(multiplexer_8_out), .lt(comparator_3_lt));  // open: gt, eq
  ALUControl alucontrol_1 (
    .ALUOp(rom_1_data[11:8]), .Func(mipsprogramrom_1_p2[5:0]), .InstructionOp(mipsprogramrom_1_p2[31:26]),
    .out_4(mips_alu_1_p3), .JRdetect(alucontrol_1_jrdetect));
  Multiplexer #(.enable("false")) multiplexer_9 (
    .in0(comparator_2_lt), .in1(comparator_3_lt), .out(multiplexer_9_out), .sel(mipsprogramrom_1_p2[0]));
  assign bit_extender_2_out = {{31{1'b0}}, multiplexer_9_out};  // Bit_Extender bit_extender_2
  Multiplexer #(.width(32), .enable("false")) multiplexer_10 (
    .in0(bit_extender_2_out), .in1(mips_alu_1_p5), .out(multiplexer_10_out), .sel(not_2_out));
  not not_2 (not_2_out, comparator_4_eq);
  Comparator #(.width(4)) comparator_4 (.a(4'b1101), .b(mips_alu_1_p3), .eq(comparator_4_eq));  // open: gt, lt
  Memory memory_1 (
    .address(mips_alu_1_p5), .Data(registerfile_1_p8), .Store(rom_1_data[2]), .Clock(clock_1_out),
    .Load(rom_1_data[3]), .BW(1'b0), .out_7(memory_1_out_7));
  Multiplexer #(.width(32), .enable("false")) multiplexer_11 (
    .in0(multiplexer_10_out), .in1(memory_1_out_7), .out(multiplexer_11_out), .sel(rom_1_data[5]));
  Multiplexer #(.width(32), .enable("false")) multiplexer_12 (
    .in0(multiplexer_11_out), .in1(adder_2_out), .out(registerfile_1_p1), .sel(rom_1_data[0]));

  // Notes on the sheet:
  //   contents of mipsprogramrom_1 (hex, n*v repeats v):
  //   addiu   $t0, $zero, 5       # $t0 = 0 + 5     addiu   $t1, $zero, 7       # $t1 = 0 + 7     addiu
  //   $s0, $zero, 9       # $s0 = 0 + 9     addiu   $s1, $zero, 2       # $s1 = 0 + 2      jal func_plus
  //   sll $t2, $t0, 1     srl $t2, $t0, 1     sra $t2, $t0, 1     j 0x200000 func_plus:     addu $t2, $t0,
  //   $t1           # $t2 = $t0 + $t1 = 12 (c)     addu $s2, $s0, $s1           # $s2 = $s0 + $s1 = 11 (b)
  //   sltiu $t3, $t2, 20           # if $t2 < 20 then $t3 = 1,else 0     beq $t3, $zero, bistwise_2   # if
  //   $t3 != 0 then go to exit     slti $t3, $t2, 4             # if $t2 < 4 then $t3 = 1,else 0     subu
  //   $t2, $t0, $t1           # $t2 = $t0 - $t1 = -2     sltu $t3, $t2, $t0           # if $t2 < $t0 then
  //   $t3 = 1,else 0     bne $t3, $zero, bistwise     # if $t3 != 0 then go to bistwise     slt $t3, $t0,
  //   $t1            # if $t0 < $t1 then $t3 = 1,else 0     bne $t3, $zero, bistwise     # if $t3 = 0 then
  //   go to bistwise  load_store:     addiu $sp, $sp, -8           # add strack     sw $t0, 4($sp)
  //   # store $t0 in 0($sp)     sw $t1, 0($sp)               # store $t1 in 0($sp)     lw $t3, 4($sp)
  //   # load $t0 to $t3     lw $t4, 0($sp)               # load $t1 to $t4     addiu $sp, $sp, 8
  //   # return strack     j bistwise_2  bistwise:     and $t4, $t0, $t1     or $t5, $t0, $t1     xor $t6,
  //   $t0, $t1     nor $t7, $t0, $t1     j load_store   bistwise_2:     andi $t4, $t0, 12     ori $t5,
  //   $t0, 13     xori $t6, $t0, 14     jr $ra
  //   Opcode
  //   RS
  //   RT
  //   RD
  //   CHUM
  //   contents of rom_1 (hex, n*v repeats v):
  //   90 0 1 91 912 a12 0 0 0 150 550 550 250 350 450 20*0 b78 7*0 c44
  //   Immediate
endmodule

module Sign_Extend (
  input  [31:0] in_1,
  output [31:0] out_2
);


  assign out_2 = {{17{in_1[15]}}, in_1[14:0]};
endmodule

module Memory (
  input  [31:0] address,
  input  [31:0] Data,
  input  Store,
  input  Clock,
  input  Load,
  input  BW,
  output [31:0] out_7
);

  wire [3:0] dmux_1_out_2, multiplexer_1_out;
  wire [4:3] bit_extender_1_out;
  wire [25:2] bit_extender_1_out_2;
  wire [31:0] shifter_1_out;

  Shifter #(.width(32)) shifter_1 (.in(Data), .\dist ({bit_extender_1_out, 3'b000}), .out(shifter_1_out));
  Bit_Extender #(.in_width(32), .out_width(26)) bit_extender_1 (
    .in(address), .out({bit_extender_1_out_2, bit_extender_1_out}));
  DMUX dmux_1 (.in_1(bit_extender_1_out), .out_2(dmux_1_out_2));
  Multiplexer #(.width(4), .enable("false")) multiplexer_1 (
    .in0(4'b1111), .in1(dmux_1_out_2), .out(multiplexer_1_out), .sel(BW));
  // MIPS_RAM #(.addrWidth(24)) mips_ram_1: pin names not known; wires that end beside it: bit_extender_1_out_2, shifter_1_out, Store, multiplexer_1_out, Clock, Load, out_7
endmodule

module DMUX (
  input  [1:0] in_1,
  output [3:0] out_2
);

  wire not_1_out, not_2_out, not_3_out, not_4_out;

  and and_1 (out_2[3], in_1[0], in_1[1]);
  not not_1 (not_1_out, in_1[1]);
  not not_2 (not_2_out, in_1[0]);
  not not_3 (not_3_out, in_1[0]);
  not not_4 (not_4_out, in_1[1]);
  and and_2 (out_2[1], in_1[0], not_1_out);
  and and_3 (out_2[2], not_2_out, in_1[1]);
  and and_4 (out_2[0], not_3_out, not_4_out);
endmodule

module LoadWord (
  input  [4:0] in_1,
  input  [4:0] in_2
);

  // AND_Gate and_1 has open pins: in0=in_1, in1=in_2, out=open
endmodule

module ALUControl (
  input  [3:0] ALUOp,
  input  [5:0] Func,
  input  [5:0] InstructionOp,
  output [3:0] out_4,
  output JRdetect
);

  wire comparator_1_eq, comparator_2_eq, comparator_3_eq, not_1_out;
  wire [3:0] Other_data, R_Type_data;

  Comparator #(.width(4)) comparator_1 (.a(4'b0000), .b(ALUOp), .eq(comparator_1_eq));  // open: gt, lt
  not not_1 (not_1_out, comparator_1_eq);
  ROM #(.addrWidth(6), .dataWidth(4)) R_Type (.addr(Func), .data(R_Type_data));
  Comparator #(.width(6)) comparator_2 (.a(InstructionOp), .b({6{1'b0}}), .eq(comparator_2_eq));  // open: gt, lt
  Comparator #(.width(6)) comparator_3 (.a(Func), .b(6'b001000), .eq(comparator_3_eq));  // open: gt, lt
  Multiplexer #(.width(4), .enable("false")) multiplexer_1 (
    .in0(R_Type_data), .in1(Other_data), .out(out_4), .sel(not_1_out));
  and and_1 (JRdetect, comparator_2_eq, comparator_3_eq);
  ROM #(.addrWidth(4), .dataWidth(4)) Other (.addr(ALUOp), .data(Other_data));

  // Notes on the sheet:
  //   contents of R_Type (hex, n*v repeats v):
  //   0 0 4 5 28*0 2 2 6 6 8 a c e 0 0 f d
  //   contents of Other (hex, n*v repeats v):
  //   0 2 8 a c d 0 0 0 b 9 2 2
endmodule
