// Logisim project Opal.circ as structural Verilog: 13 circuits, main circuit main
module main (
  input  in_1,
  output [4:0] out_2
);

  wire ALUSrc, Branch, Branch_EXE, clk, MemtoReg, RegWrite, RegWrite_MEM_WB;
  wire [1:0] exe_mem_1_mem_o, id_ex_1_mem_o, MEM_T, mem_wb_1_wb_o;
  wire [2:0] ALUOp, exe_mem_1_wb_o, id_ex_1_wb_o;
  wire [4:0] exe_1_rw, exe_mem_1_rw_o;
  wire [5:0] id_1_inst5_0, id_ex_1_inst5_0_o;
  wire [6:0] ALUControl_data, ALUControlzzz;
  wire [10:0] EXE_T, id_ex_1_exe_o;
  wire [31:0] exe_1_aluresult, exe_1_nextpc_b, exe_mem_1_aluresult_o, exe_mem_1_nextpc_o, exe_mem_1_pc_4_o,
       exe_mem_1_rt_o, id_1_inst, id_1_inst15_0_ex_32, id_1_rs, id_1_rt, id_ex_1_a_o, id_ex_1_b_o,
       id_ex_1_inst15_0_ex_32_o, id_ex_1_inst_o, id_ex_1_pc_4_o, if_1_instruction, if_1_pc_4,
       if_id_1_instruction_o, if_id_1_pc_4_o, mem_1_memresult, mem_wb_1_aluresult_o, mem_wb_1_memresult_o,
       mem_wb_1_pc_4_o, multiplexer_1_out, multiplexer_2_out, multiplexer_3_out, nextpc_EXE, WriteData;

  Clock clock_1 (.out(clk));
  IF if_1 (.nextpc(multiplexer_2_out), .Clock(clk), .Reset(in_1), .Instruction(if_1_instruction), .PC_4(if_1_pc_4));
  Multiplexer #(.width(32), .enable("false")) multiplexer_1 (
    .in0(if_1_pc_4), .in1(nextpc_EXE), .out(multiplexer_1_out), .sel(Branch_EXE));
  IF_ID if_id_1 (
    .Instruction(if_1_instruction), .PC_4(if_1_pc_4), .clk(clk), .Instruction_o(if_id_1_instruction_o),
    .PC_4_o(if_id_1_pc_4_o));
  ROM #(.addrWidth(6), .dataWidth(11)) ControlUnit (
    .addr(if_id_1_instruction_o[31:26]),
    .data({Branch, EXE_T[0], RegWrite, ALUSrc, MEM_T[0], ALUOp, MemtoReg, MEM_T[1], EXE_T[10]}));
  Multiplexer #(.width(32), .enable("false")) multiplexer_2 (
    .in0(multiplexer_3_out), .in1(id_ex_1_a_o), .out(multiplexer_2_out), .sel(ALUControlzzz[6]));
  // RegisterFile #(.trigger("falling")) registerfile_1: pin names not known; wires that end beside it: WriteData, clk, RegWrite_MEM_WB, out_2
  ID id_1 (
    .Instruction(if_id_1_instruction_o), .clk(clk), .WriteData(WriteData), .RegWrite(RegWrite_MEM_WB),
    .rW(out_2), .Inst(id_1_inst), .Inst5_0(id_1_inst5_0), .Inst15_0_ex_32(id_1_inst15_0_ex_32), .rs(id_1_rs),
    .rt(id_1_rt));
  Multiplexer #(.width(32), .enable("false")) multiplexer_3 (
    .in0(multiplexer_1_out), .in1({id_ex_1_pc_4_o[31:28], if_1_instruction[25:0], 2'b00}),
    .out(multiplexer_3_out), .sel(id_ex_1_wb_o[1]));
  ROM #(.addrWidth(6), .dataWidth(7)) ALUControl (.addr(id_ex_1_inst5_0_o), .data(ALUControl_data));
  Multiplexer #(.select(3), .width(7), .enable("false")) multiplexer_4 (
    .in0(7'b0000010), .in1(7'b0001011), .in2(7'b0001001), .in3(ALUControl_data), .in4(7'b0001000),
    .in5(7'b0001010), .in6(7'b0001100), .in7(7'b0001111), .out(ALUControlzzz), .sel(ALUOp));
  ID_EX id_ex_1 (
    .PC_4(if_id_1_pc_4_o), .A(id_1_rs), .B(id_1_rt), .Inst(id_1_inst), .Inst5_0(id_1_inst5_0),
    .Inst15_0_ex_32(id_1_inst15_0_ex_32), .WB({RegWrite, EXE_T[0], MemtoReg}),
    .EXE({EXE_T[10], ALUControlzzz, ALUSrc, Branch, EXE_T[0]}), .MEM(MEM_T), .clk(clk),
    .PC_4_O(id_ex_1_pc_4_o), .A_O(id_ex_1_a_o), .B_O(id_ex_1_b_o), .Inst_o(id_ex_1_inst_o),
    .Inst5_0_O(id_ex_1_inst5_0_o), .Inst15_0_ex_32_O(id_ex_1_inst15_0_ex_32_o), .WB_O(id_ex_1_wb_o),
    .EXE_O(id_ex_1_exe_o), .MEM_O(id_ex_1_mem_o));
  EXE exe_1 (
    .PC_4(id_ex_1_pc_4_o), .Instruction(id_ex_1_inst_o), .A(id_ex_1_a_o), .B(id_ex_1_b_o),
    .Inst15_0_ex_32(id_ex_1_inst15_0_ex_32_o), .EXE(id_ex_1_exe_o), .nextpc(nextpc_EXE),
    .NextPC_B(exe_1_nextpc_b), .ALUResult(exe_1_aluresult), .rW(exe_1_rw), .Branch_O(Branch_EXE));
  EXE_MEM exe_mem_1 (
    .WB(id_ex_1_wb_o), .ALUResult_O(exe_mem_1_aluresult_o), .MEM(id_ex_1_mem_o), .MEM_O(exe_mem_1_mem_o),
    .ALUResult(exe_1_aluresult), .WB_O(exe_mem_1_wb_o), .nextpc(exe_1_nextpc_b), .clk(clk), .rt(id_ex_1_b_o),
    .rW(exe_1_rw), .nextpc_O(exe_mem_1_nextpc_o), .rt_O(exe_mem_1_rt_o), .rW_O(exe_mem_1_rw_o),
    .PC_4(id_ex_1_pc_4_o), .PC_4_O(exe_mem_1_pc_4_o));
  MEM mem_1 (
    .ALUresult(exe_mem_1_aluresult_o), .DATAfromRT(exe_mem_1_rt_o), .clk(clk), .MEM(exe_mem_1_mem_o),
    .MemResult(mem_1_memresult));
  MEM_WB mem_wb_1 (
    .PC_4(exe_mem_1_pc_4_o), .WB(exe_mem_1_wb_o), .MemResult(mem_1_memresult),
    .ALUResult(exe_mem_1_aluresult_o), .rW(exe_mem_1_rw_o), .clk(clk), .PC_4_O(mem_wb_1_pc_4_o),
    .WB_O({RegWrite_MEM_WB, mem_wb_1_wb_o}), .MemResult_O(mem_wb_1_memresult_o),
    .ALUResult_o(mem_wb_1_aluresult_o), .rW_O(out_2));
  WB wb_1 (
    .MemResult(mem_wb_1_memresult_o), .ALUResult(mem_wb_1_aluresult_o), .PC_4(mem_wb_1_pc_4_o),
    .WB({RegWrite_MEM_WB, mem_wb_1_wb_o}), .WriteData(WriteData));

  // Other names for the same wires on the sheet: RegDst = EXE_T[10]; MemRead = MEM_T[1];
  //   WB_T[2:0] = {RegWrite, EXE_T[0], MemtoReg}; MemWrite = MEM_T[0]; EXE_T[9:1] = {ALUControlzzz, ALUSrc, Branch};
  //   Jump = EXE_T[0]; rW[4:0] = out_2

  // Notes on the sheet:
  //   contents of ControlUnit (hex, n*v repeats v):
  //   119 0 200 300 408 410 0 0 0 180 1b8 1b8 1a0 1a8 1b0 20*0 186 7*0 c2
  //   contents of ALUControl (hex, n*v repeats v):
  //   10 0 14 15 4*0 40 24*0 2 0 6 8 a c e 0 0 20 20
endmodule

module Demux (
  input  [1:0] in_1,
  output [3:0] out_2
);

  wire not_1_out, not_2_out, not_3_out, not_4_out;

  and and_1 (out_2[3], in_1[1], in_1[0]);
  not not_1 (not_1_out, in_1[0]);
  not not_2 (not_2_out, in_1[1]);
  not not_3 (not_3_out, in_1[1]);
  not not_4 (not_4_out, in_1[0]);
  and and_2 (out_2[2], in_1[1], not_1_out);
  and and_3 (out_2[1], not_2_out, in_1[0]);
  and and_4 (out_2[0], not_3_out, not_4_out);
endmodule

module Shift (
  input  S,
  input  [31:0] D,
  input  [1:0] sel,
  output [31:0] t0
);

  wire [4:0] bit_extender_1_out;
  wire [31:0] shifter_1_out, shifter_2_out, shifter_3_out;

  assign bit_extender_1_out = {{4{S}}, S};  // Bit_Extender bit_extender_1
  Shifter #(.width(32)) shifter_1 (.in(D), .\dist (bit_extender_1_out), .out(shifter_1_out));
  Shifter #(.width(32), .shift("lr")) shifter_2 (.in(D), .\dist (bit_extender_1_out), .out(shifter_2_out));
  Shifter #(.width(32), .shift("ar")) shifter_3 (.in(D), .\dist (bit_extender_1_out), .out(shifter_3_out));
  Multiplexer #(.select(2), .width(32), .enable("false")) multiplexer_1 (
    .in0(shifter_1_out), .in1(shifter_2_out), .in2(shifter_3_out), .out(t0), .sel(sel));  // open: in3
endmodule

module ALU (
  input  [4:0] shampt,
  input  [31:0] A,
  input  [31:0] B,
  input  [3:0] op,
  input  slt,
  output [31:0] C
);

  wire and_1_out, comparator_1_lt, or_1_out;
  wire [31:0] bit_extender_1_out, mips_alu_1_p5;

  // Mips_ALU mips_alu_1: pin names not known; wires that end beside it: A, B, op, shampt, mips_alu_1_p5, A
  and and_1 (and_1_out, op[0], op[1], op[3], op[2]);
  or or_1 (or_1_out, and_1_out, slt);
  Comparator #(.width(32)) comparator_1 (.a(A), .b(B), .lt(comparator_1_lt));  // open: gt, eq
  assign bit_extender_1_out = {{31{1'b0}}, comparator_1_lt};  // Bit_Extender bit_extender_1
  Multiplexer #(.width(32), .enable("false")) multiplexer_1 (
    .in0(mips_alu_1_p5), .in1(bit_extender_1_out), .out(C), .sel(or_1_out));
endmodule

module IF (
  input  [31:0] nextpc,
  input  Clock,
  input  Reset,
  output [31:0] Instruction,
  output [31:0] PC_4
);

  wire [31:0] register_1_q;

  Register #(.width(32)) register_1 (.D(nextpc), .en(1'b1), .clk(Clock), .Q(register_1_q), .clr(Reset));
  // MIPSProgramROM mipsprogramrom_1: pin names not known; wires that end beside it: register_1_q, Instruction
  Adder #(.width(32)) adder_1 (.a(32'h4), .b(register_1_q), .out(PC_4));  // open: cin, cout

  // Notes on the sheet:
  //   contents of mipsprogramrom_1 (hex, n*v repeats v):
  //   addiu   $t0, $zero, 5           #5                      # $t0 = 0 + 5     addiu   $t1, $zero, 7
  //   #6                      # $t1 = 0 + 7     addiu   $s0, $zero, 9           #7                      #
  //   $s0 = 0 + 9     addiu   $s1, $zero, 2           #8                      # $s1 = 0 + 2     addu
  //   $s5, $zero, $zero           #9                          # $s5 = 0 + 0     addiu $s6, $zero, 5
  //   #10                             # $s6 = 0 + 4     jal func_plus                   #11     sll $t2,
  //   $t0, 1                 #128     srl $t2, $t0, 1                 #129     sra $t2, $t0, 1
  //   #130     j 0x200000                      #131 func_plus:     addu $s2, $s0, $s1              #12
  //   # $s2 = $s0 + $s1 = 11 (b)     addu $t2, $t0, $t1              #13                     # $t2 = $t0 +
  //   $t1 = 12 (c)     nop     nop     sltiu $t3, $t2, 20              #16                     # if $t2 <
  //   20 then $t3 = 1,else 0     nop     nop     beq  $t3, $zero, bistwise_2                             #
  //   if $t3 != 0 then go to exit     slti $t3, $t2, 4                                        # if $t2 < 4
  //   then $t3 = 1,else 0     subu $t2, $t0, $t1              #21                     # $t2 = $t0 - $t1 =
  //   -2     nop     nop     sltu $t3, $t2, $t0                                      # if $t2 < $t0 then
  //   $t3 = 1,else 0     nop     nop     bne $t3, $zero, bistwise                                # if $t3
  //   != 0 then go to bistwise     slt $t3, $t0, $t1                                       # if $t0 < $t1
  //   then $t3 = 1,else 0     nop     nop     bne $t3, $zero, bistwise        #31                     # if
  //   $t3 = 0 then go to bistwise  load_store:     addiu $sp, $sp, -8              #37 #56 #75 #94 #113
  //   # add strack     sw $t0, 4($sp)                                          # store $t0 in 0($sp)
  //   sw $t1, 0($sp)                                          # store $t1 in 0($sp)     nop     nop     lw
  //   $t3, 4($sp)                                          # load $t0 to $t3     lw $t4, 0($sp)
  //   # load $t1 to $t4     addiu $sp, $sp, 8                                       # return strack     j
  //   bistwise_2                    #45 #64 #83 #102 #121  bistwise:     and $t4, $t0, $t1
  //   #32 #51 #70 #89 #108     or  $t5, $t0, $t1               #33     xor $t6, $t0, $t1               #34
  //   nor $t7, $t0, $t1               #35     j load_store                    #36 #55 #74 #93 #112
  //   bistwise_2:     andi $t4, $t0, 12               #46 #65 #84 #103 #122     ori  $t5, $t0, 13     xori
  //   $t6, $t0, 14     addiu $s5, $s5, 1                #49  #68 #87 #106 #125     bne  $s5, $s6, bistwise
  //   #50 #69 #88 #107 #126     jr $ra                          #127
endmodule

module MEM (
  input  [31:0] ALUresult,
  input  [31:0] DATAfromRT,
  input  clk,
  input  [1:0] MEM,
  output [31:0] MemResult
);

  wire [25:0] bit_extender_1_out;

  Bit_Extender #(.in_width(32), .out_width(26)) bit_extender_1 (.in(ALUresult), .out(bit_extender_1_out));
  // MIPS_RAM #(.addrWidth(24)) mips_ram_1: pin names not known; wires that end beside it: bit_extender_1_out[25:2], DATAfromRT, MEM[0], MEM[0], 4'b1111, clk, MEM[1], MEM[1], 1'b0, MemResult

  // Other names for the same wires on the sheet: MemWrite = MEM[0]; MemRead = MEM[1]
endmodule

module ID (
  input  [31:0] Instruction,
  input  clk,
  input  [31:0] WriteData,
  input  RegWrite,
  input  [4:0] rW,
  output [31:0] Inst,
  output [5:0] Inst5_0,
  output [31:0] Inst15_0_ex_32,
  output [31:0] rs,
  output [31:0] rt
);

  assign Inst15_0_ex_32 = {{16{Instruction[15]}}, Instruction[15:0]};  // Bit_Extender bit_extender_1
  // RegisterFile #(.trigger("falling")) registerfile_1: pin names not known; wires that end beside it: WriteData, clk, RegWrite, rW, Instruction[25:21], Instruction[20:16], rs, rt

  assign Inst = Instruction;
  assign Inst5_0 = Instruction[5:0];

  // Other names for the same wires on the sheet: Inst15_11[4:0] = Instruction[15:11];
  //   Inst20_16[4:0] = Instruction[20:16]; Inst25_21[4:0] = Instruction[25:21]

  // Notes on the sheet:
  //   rs
  //   rt
endmodule

module WB (
  input  [31:0] MemResult,
  input  [31:0] ALUResult,
  input  [31:0] PC_4,
  input  [2:0] WB,
  output [31:0] WriteData
);

  wire [31:0] multiplexer_1_out;

  Multiplexer #(.width(32), .enable("false")) multiplexer_1 (
    .in0(ALUResult), .in1(MemResult), .out(multiplexer_1_out), .sel(WB[0]));
  Multiplexer #(.width(32), .enable("false")) multiplexer_2 (
    .in0(multiplexer_1_out), .in1(PC_4), .out(WriteData), .sel(WB[1]));

  // Other names for the same wires on the sheet: MemtoReg = WB[0]; Jump = WB[1]
endmodule

module EXE (
  input  [31:0] PC_4,
  input  [31:0] Instruction,
  input  [31:0] A,
  input  [31:0] B,
  input  [31:0] Inst15_0_ex_32,
  input  [10:0] EXE,
  output [31:0] nextpc,
  output [31:0] NextPC_B,
  output [31:0] ALUResult,
  output [4:0] rW,
  output Branch_O
);

  wire and_1_out, bit_extender_1_out;
  wire [4:0] multiplexer_4_out;
  wire [25:0] undriven;
  wire [31:0] multiplexer_1_out, multiplexer_3_out, shifter_1_out, undriven_2;

  Multiplexer #(.width(32), .enable("false")) multiplexer_1 (
    .in0(B), .in1(Inst15_0_ex_32), .out(multiplexer_1_out), .sel(EXE[2]));
  Multiplexer #(.width(32), .enable("false")) multiplexer_2 (
    .in0(multiplexer_3_out), .in1(A), .out(nextpc), .sel(EXE[9]));
  Adder #(.width(32)) adder_1 (.a(PC_4), .b(shifter_1_out), .out(NextPC_B));  // open: cin, cout
  Shifter #(.width(32)) shifter_1 (.in(Inst15_0_ex_32), .\dist (5'b00010), .out(shifter_1_out));
  ALU alu_1 (.shampt(Inst15_0_ex_32[10:6]), .A(A), .B(multiplexer_1_out), .op(EXE[6:3]), .slt(EXE[8]), .C(ALUResult));
  and and_1 (and_1_out, EXE[1], bit_extender_1_out);
  Bit_Extender #(.in_width(32), .out_width(1)) bit_extender_1 (.in(ALUResult), .out(bit_extender_1_out));
  Multiplexer #(.width(32), .enable("false")) multiplexer_3 (
    .in0(undriven_2), .in1({PC_4[31:28], undriven, 2'b00}), .out(multiplexer_3_out), .sel(EXE[0]));
  Multiplexer #(.width(5), .enable("false")) multiplexer_4 (
    .in0(Instruction[20:16]), .in1(Instruction[15:11]), .out(multiplexer_4_out), .sel(EXE[10]));
  Multiplexer #(.width(5), .enable("false")) multiplexer_5 (
    .in0(multiplexer_4_out), .in1({5{1'b1}}), .out(rW), .sel(EXE[0]));

  assign Branch_O = EXE[1];

  // Other names for the same wires on the sheet: Jump = EXE[0]; Branch = EXE[1]; ALUSrc = EXE[2];
  //   ALUControlzzz[6:0] = EXE[9:3]; jr = EXE[9]; RegDst = EXE[10]
endmodule

module IF_ID (
  input  [31:0] Instruction,
  input  [31:0] PC_4,
  input  clk,
  output [31:0] Instruction_o,
  output [31:0] PC_4_o
);

  Register #(.width(32)) register_1 (.D(Instruction), .en(1'b1), .clk(clk), .Q(Instruction_o), .clr(1'b0));
  Register #(.width(32)) register_2 (.D(PC_4), .en(1'b1), .clk(clk), .Q(PC_4_o), .clr(1'b0));
endmodule

module ID_EX (
  input  [31:0] PC_4,
  input  [31:0] A,
  input  [31:0] B,
  input  [31:0] Inst,
  input  [5:0] Inst5_0,
  input  [31:0] Inst15_0_ex_32,
  input  [2:0] WB,
  input  [10:0] EXE,
  input  [1:0] MEM,
  input  clk,
  output [31:0] PC_4_O,
  output [31:0] A_O,
  output [31:0] B_O,
  output [31:0] Inst_o,
  output [5:0] Inst5_0_O,
  output [31:0] Inst15_0_ex_32_O,
  output [2:0] WB_O,
  output [10:0] EXE_O,
  output [1:0] MEM_O
);

  Register #(.width(32)) register_1 (.D(PC_4), .en(1'b1), .clk(clk), .Q(PC_4_O));  // open: clr
  Register #(.width(32)) register_2 (.D(A), .en(1'b1), .clk(clk), .Q(A_O));  // open: clr
  Register #(.width(32)) register_3 (.D(B), .en(1'b1), .clk(clk), .Q(B_O));  // open: clr
  Register #(.width(32)) register_4 (.D(Inst), .en(1'b1), .clk(clk), .Q(Inst_o));  // open: clr
  Register #(.width(6)) register_5 (.D(Inst5_0), .en(1'b1), .clk(clk), .Q(Inst5_0_O));  // open: clr
  Register #(.width(32)) register_6 (.D(Inst15_0_ex_32), .en(1'b1), .clk(clk), .Q(Inst15_0_ex_32_O));  // open: clr
  Register #(.width(3)) register_7 (.D(WB), .en(1'b1), .clk(clk), .Q(WB_O));  // open: clr
  Register #(.width(11)) register_8 (.D(EXE), .en(1'b1), .clk(clk), .Q(EXE_O));  // open: clr
  Register #(.width(2)) register_9 (.D(MEM), .en(1'b1), .clk(clk), .Q(MEM_O));  // open: clr
endmodule

module EXE_MEM (
  input  [31:0] PC_4,
  input  [2:0] WB,
  input  [1:0] MEM,
  input  [31:0] ALUResult,
  input  [31:0] nextpc,
  input  [31:0] rt,
  input  [4:0] rW,
  input  clk,
  output [31:0] PC_4_O,
  output [2:0] WB_O,
  output [1:0] MEM_O,
  output [31:0] ALUResult_O,
  output [31:0] nextpc_O,
  output [31:0] rt_O,
  output [4:0] rW_O
);

  Register #(.width(32)) register_1 (.D(PC_4), .en(1'b1), .clk(clk), .Q(PC_4_O));  // open: clr
  Register #(.width(3)) register_2 (.D(WB), .en(1'b1), .clk(clk), .Q(WB_O));  // open: clr
  Register #(.width(2)) register_3 (.D(MEM), .en(1'b1), .clk(clk), .Q(MEM_O));  // open: clr
  Register #(.width(32)) register_4 (.D(ALUResult), .en(1'b1), .clk(clk), .Q(ALUResult_O));  // open: clr
  Register #(.width(32)) register_5 (.D(nextpc), .en(1'b1), .clk(clk), .Q(nextpc_O));  // open: clr
  Register #(.width(32)) register_6 (.D(rt), .en(1'b1), .clk(clk), .Q(rt_O));  // open: clr
  Register #(.width(5)) register_7 (.D(rW), .en(1'b1), .clk(clk), .Q(rW_O));  // open: clr

  // Other names for the same wires on the sheet: MemWrite = MEM[0]; MemRead = MEM[1]
endmodule

module MEM_WB (
  input  [31:0] PC_4,
  input  [2:0] WB,
  input  [31:0] MemResult,
  input  [31:0] ALUResult,
  input  [4:0] rW,
  input  clk,
  output [31:0] PC_4_O,
  output [2:0] WB_O,
  output [31:0] MemResult_O,
  output [31:0] ALUResult_o,
  output [4:0] rW_O
);

  Register #(.width(32)) register_1 (.D(PC_4), .en(1'b1), .clk(clk), .Q(PC_4_O));  // open: clr
  Register #(.width(3)) register_2 (.D(WB), .en(1'b1), .clk(clk), .Q(WB_O));  // open: clr
  Register #(.width(32)) register_3 (.D(MemResult), .en(1'b1), .clk(clk), .Q(MemResult_O));  // open: clr
  Register #(.width(32)) register_4 (.D(ALUResult), .en(1'b1), .clk(clk), .Q(ALUResult_o));  // open: clr
  Register #(.width(5)) register_5 (.D(rW), .en(1'b1), .clk(clk), .Q(rW_O));  // open: clr
endmodule
