// Logisim project mips_pipeline.circ as structural Verilog
// ALU
module main (
  input  in_1
);

  wire alucontrol_1_jrdetect, and_1_out, clock_1_out, comparator_1_eq, deandexe3_1_out_9, deandexe3_1_out_10,
       deandexe3_1_out_11, deandexe3_1_out_12, deandexe3_1_out_13, deandexe3_1_out_14,
       deandexe_1_out_alu_src, exandmem_1_out_12, exandmem_1_out_13, exandmem_1_out_14, exandmem_1_out_15,
       exandmem_1_out_19, memandwb_1_out_9, memandwb_1_out_11, mips_alu_1_p1, not_1_out, registerfile_1_p3;
  wire [1:0] register_1_q;
  wire [3:0] alucontrol_1_out_4, deandexe2_1_out_5;
  wire [4:0] deandexe2_1_out_6, deandexe_1_out_rw, exandmem_1_out_21, ifandde_1_out_instruction_2,
       ifandde_1_out_instruction_3, ifandde_1_out_instruction_4, ifandde_1_out_instruction_5,
       multiplexer_4_out, multiplexer_5_out, multiplexer_6_out, registerfile_1_p4;
  wire [5:0] deandexe2_1_out_7, deandexe_1_out_8, ifandde_1_out_instruction, ifandde_1_out_instruction_6;
  wire [11:0] rom_1_data;
  wire [29:0] incrementer_1_p1, incrementer_1_p3;
  wire [31:0] adder_1_out, aluunsign_1_out_6, bit_extender_1_out, deandexe3_1_out_15, deandexe_1_out_a,
       deandexe_1_out_b, deandexe_1_out_imediate, exandmem_1_out_16, exandmem_1_out_17, exandmem_1_out_18,
       exandmem_1_out_20, ifandde_1_out_pc4, memandwb_1_out_12, memandwb_1_out_13, memandwb_1_out_14,
       memory_1_out_7, mips_alu_1_p8, mipsprogramrom_1_p2, multiplexer_1_out, multiplexer_2_out,
       multiplexer_3_out, multiplexer_7_out, multiplexer_8_out, multiplexer_9_out, registerfile_1_p1,
       registerfile_1_p7, registerfile_1_p8, shifter_1_out, shifter_2_out, sign_extend_1_out_2;

  Multiplexer #(.width(32), .enable("false")) multiplexer_1 (
    .in0(multiplexer_2_out), .in1(registerfile_1_p7), .out(multiplexer_1_out), .sel(alucontrol_1_jrdetect));
  Multiplexer #(.width(32), .enable("false")) multiplexer_2 (
    .in0(multiplexer_3_out), .in1(shifter_1_out), .out(multiplexer_2_out), .sel(rom_1_data[0]));
  Clock clock_1 (.out(clock_1_out));
  Multiplexer #(.width(32), .enable("false")) multiplexer_3 (
    .in0({incrementer_1_p3, 2'b00}), .in1(adder_1_out), .out(multiplexer_3_out), .sel(and_1_out));
  // Incrementer #(.width(30)) incrementer_1: pin names not known; wires that end beside it: incrementer_1_p1, clock_1_out, incrementer_1_p3
  Register #(.width(32), .trigger("falling")) register_1 (
    .D(multiplexer_1_out), .clk(clock_1_out), .Q({incrementer_1_p1, register_1_q}), .clr(in_1));  // open: en
  // MIPSProgramROM mipsprogramrom_1: pin names not known; wires that end beside it: {incrementer_1_p1, register_1_q}, mipsprogramrom_1_p2
  assign bit_extender_1_out = {{6{ifandde_1_out_instruction_5[4]}}, {ifandde_1_out_instruction_5, ifandde_1_out_instruction_4, ifandde_1_out_instruction_3, ifandde_1_out_instruction_2, ifandde_1_out_instruction}};  // Bit_Extender bit_extender_1
  IFandDe ifandde_1 (
    .PC4({incrementer_1_p3, 2'b00}), .Instruction(mipsprogramrom_1_p2), .CLK(clock_1_out),
    .Out_PC4(ifandde_1_out_pc4),
    .Out_Instruction({ifandde_1_out_instruction_6, ifandde_1_out_instruction_5, ifandde_1_out_instruction_4, ifandde_1_out_instruction_3, ifandde_1_out_instruction_2, ifandde_1_out_instruction}));
  Shifter #(.width(32)) shifter_1 (.in(bit_extender_1_out), .\dist (5'b00010), .out(shifter_1_out));
  ROM #(.addrWidth(6), .dataWidth(12)) rom_1 (.addr(ifandde_1_out_instruction_6), .data(rom_1_data));
  Sign_Extend sign_extend_1 (
    .in_1({ifandde_1_out_instruction_6, ifandde_1_out_instruction_5, ifandde_1_out_instruction_4, ifandde_1_out_instruction_3, ifandde_1_out_instruction_2, ifandde_1_out_instruction}),
    .out_2(sign_extend_1_out_2));
  Multiplexer #(.width(5), .enable("false")) multiplexer_4 (
    .in0(ifandde_1_out_instruction_5), .in1({5{1'b1}}), .out(multiplexer_4_out), .sel(alucontrol_1_jrdetect));
  Multiplexer #(.width(5), .enable("false")) multiplexer_5 (
    .in0(ifandde_1_out_instruction_4), .in1(ifandde_1_out_instruction_3), .out(multiplexer_5_out),
    .sel(rom_1_data[7]));
  Multiplexer #(.width(5), .enable("false")) multiplexer_6 (
    .in0(multiplexer_5_out), .in1({5{1'b1}}), .out(multiplexer_6_out), .sel(rom_1_data[0]));
  // RegisterFile #(.trigger("falling")) registerfile_1: pin names not known; wires that end beside it: registerfile_1_p1, clock_1_out, registerfile_1_p3, registerfile_1_p4, multiplexer_4_out, ifandde_1_out_instruction_4, registerfile_1_p7, registerfile_1_p8
  ALUControl alucontrol_1 (
    .ALUOp(rom_1_data[11:8]), .Func(ifandde_1_out_instruction), .InstructionOp(ifandde_1_out_instruction_6),
    .out_4(alucontrol_1_out_4), .JRdetect(alucontrol_1_jrdetect));
  DeandExe3 deandexe3_1 (
    .a0(rom_1_data[0]), .a1(rom_1_data[1]), .a2(rom_1_data[2]), .a3(rom_1_data[3]), .a4(rom_1_data[4]),
    .a5(rom_1_data[5]), .PC4(ifandde_1_out_pc4), .CLK(clock_1_out), .out_9(deandexe3_1_out_9),
    .out_10(deandexe3_1_out_10), .out_11(deandexe3_1_out_11), .out_12(deandexe3_1_out_12),
    .out_13(deandexe3_1_out_13), .out_14(deandexe3_1_out_14), .out_15(deandexe3_1_out_15));
  DeandExe deandexe_1 (
    .Opcode(ifandde_1_out_instruction_6), .A(registerfile_1_p7), .B(registerfile_1_p8),
    .RW(multiplexer_6_out), .Imediate(sign_extend_1_out_2), .ALU_Src(rom_1_data[6]), .CLK(clock_1_out),
    .out_8(deandexe_1_out_8), .Out_A(deandexe_1_out_a), .Out_B(deandexe_1_out_b), .Out_RW(deandexe_1_out_rw),
    .Out_Imediate(deandexe_1_out_imediate), .Out_ALU_Src(deandexe_1_out_alu_src));
  DeandExe2 deandexe2_1 (
    .ALU_Op(alucontrol_1_out_4), .Chem(ifandde_1_out_instruction_2), .Func(ifandde_1_out_instruction),
    .CLK(clock_1_out), .out_5(deandexe2_1_out_5), .out_6(deandexe2_1_out_6), .out_7(deandexe2_1_out_7));
  Shifter #(.width(32)) shifter_2 (.in(deandexe_1_out_imediate), .\dist (5'b00010), .out(shifter_2_out));
  Adder #(.width(32)) adder_1 (.a(deandexe3_1_out_15), .b(shifter_2_out), .out(adder_1_out));  // open: cin, cout
  Multiplexer #(.width(32), .enable("false")) multiplexer_7 (
    .in0(deandexe_1_out_b), .in1(deandexe_1_out_imediate), .out(multiplexer_7_out),
    .sel(deandexe_1_out_alu_src));
  and and_1 (and_1_out, mips_alu_1_p8[0], deandexe3_1_out_10);
  ALUUnsign aluunsign_1 (
    .A(deandexe_1_out_a), .B(deandexe_1_out_b), .Imediate(deandexe_1_out_imediate), .Func(deandexe2_1_out_7),
    .Opcode(deandexe_1_out_8), .out_6(aluunsign_1_out_6));
  // Mips_ALU mips_alu_1: pin names not known; wires that end beside it: mips_alu_1_p1, mips_alu_1_p1, deandexe_1_out_a, multiplexer_7_out, deandexe2_1_out_5, deandexe2_1_out_5, deandexe2_1_out_6, mips_alu_1_p8
  Comparator #(.width(4)) comparator_1 (.a(4'b1101), .b(deandexe2_1_out_5), .eq(comparator_1_eq));  // open: gt, lt
  Multiplexer #(.width(32), .enable("false")) multiplexer_8 (
    .in0(aluunsign_1_out_6), .in1(mips_alu_1_p8), .out(multiplexer_8_out), .sel(not_1_out));
  not not_1 (not_1_out, comparator_1_eq);
  ExandMem exandmem_1 (
    .a0(deandexe3_1_out_9), .a2(deandexe3_1_out_11), .a3(deandexe3_1_out_12), .a5(deandexe3_1_out_14),
    .A(multiplexer_8_out), .Result(multiplexer_8_out), .B(deandexe_1_out_b), .a4(deandexe3_1_out_13),
    .PC4(deandexe3_1_out_15), .rw(deandexe_1_out_rw), .CLK(clock_1_out), .out_12(exandmem_1_out_12),
    .out_13(exandmem_1_out_13), .out_14(exandmem_1_out_14), .out_15(exandmem_1_out_15),
    .out_16(exandmem_1_out_16), .out_17(exandmem_1_out_17), .out_18(exandmem_1_out_18),
    .out_19(exandmem_1_out_19), .out_20(exandmem_1_out_20), .out_21(exandmem_1_out_21));
  Memory memory_1 (
    .address(exandmem_1_out_17), .Data(exandmem_1_out_18), .Store(exandmem_1_out_13), .CLK(clock_1_out),
    .Load(exandmem_1_out_14), .BW(1'b0), .out_7(memory_1_out_7));
  MemandWb memandwb_1 (
    .a0(exandmem_1_out_12), .a4(exandmem_1_out_19), .a5(exandmem_1_out_15), .A(exandmem_1_out_16),
    .Result(memory_1_out_7), .PC4(exandmem_1_out_20), .RW(exandmem_1_out_21), .CLK(clock_1_out),
    .out_9(memandwb_1_out_9), .out_10(registerfile_1_p3), .out_11(memandwb_1_out_11),
    .out_12(memandwb_1_out_12), .out_13(memandwb_1_out_13), .out_14(memandwb_1_out_14),
    .out_15(registerfile_1_p4));
  Multiplexer #(.width(32), .enable("false")) multiplexer_9 (
    .in0(memandwb_1_out_12), .in1(memandwb_1_out_13), .out(multiplexer_9_out), .sel(memandwb_1_out_11));
  Multiplexer #(.width(32), .enable("false")) multiplexer_10 (
    .in0(multiplexer_9_out), .in1(memandwb_1_out_14), .out(registerfile_1_p1), .sel(memandwb_1_out_9));

  // Notes on the sheet:
  //   contents of mipsprogramrom_1 (hex, n*v repeats v):
  //   addiu   $t0, $zero, 5           #5                      # $t0 = 0 + 5     addiu   $t1, $zero, 7
  //   #6                      # $t1 = 0 + 7     addiu   $s0, $zero, 9           #7                      #
  //   $s0 = 0 + 9     addiu   $s1, $zero, 2           #8                      # $s1 = 0 + 2     addu
  //   $s5, $zero, $zero           #9                          # $s5 = 0 + 0     addiu $s6, $zero, 5
  //   #10                             # $s6 = 0 + 4     jal func_plus                   #11     nop
  //   sll $t2, $t0, 1                 #128     srl $t2, $t0, 1                 #129     sra $t2, $t0, 1
  //   #130     j 0x200000                      #131 func_plus:     addu $s2, $s0, $s1              #12
  //   # $s2 = $s0 + $s1 = 11 (b)     addu $t2, $t0, $t1              #13                     # $t2 = $t0 +
  //   $t1 = 12 (c)     nop     nop     nop     sltiu $t3, $t2, 20              #16                     #
  //   if $t2 < 20 then $t3 = 1,else 0     nop     nop     nop     beq  $t3, $zero, bistwise_2
  //   # if $t3 != 0 then go to exit     nop     slti $t3, $t2, 4                                        #
  //   if $t2 < 4 then $t3 = 1,else 0     subu $t2, $t0, $t1              #21                     # $t2 =
  //   $t0 - $t1 = -2     nop     nop     nop     sltu $t3, $t2, $t0                                      #
  //   if $t2 < $t0 then $t3 = 1,else 0     nop     nop     nop     bne $t3, $zero, bistwise
  //   # if $t3 != 0 then go to bistwise     nop     slt $t3, $t0, $t1
  //   # if $t0 < $t1 then $t3 = 1,else 0     nop     nop     nop     bne $t3, $zero, bistwise        #31
  //   # if $t3 = 0 then go to bistwise  load_store:     addiu $sp, $sp, -8              #37 #56 #75 #94
  //   #113    # add strack     sw $t0, 4($sp)                                          # store $t0 in
  //   0($sp)     sw $t1, 0($sp)                                          # store $t1 in 0($sp)     nop
  //   nop     lw $t3, 4($sp)                                          # load $t0 to $t3     lw $t4, 0($sp)
  //   # load $t1 to $t4     addiu $sp, $sp, 8                                       # return strack     j
  //   bistwise_2                    #45 #64 #83 #102 #121  bistwise:     and $t4, $t0, $t1
  //   #32 #51 #70 #89 #108     or  $t5, $t0, $t1               #33     xor $t6, $t0, $t1               #34
  //   nor $t7, $t0, $t1               #35     j load_store                    #36 #55 #74 #93 #112
  //   bistwise_2:     andi $t4, $t0, 12               #46 #65 #84 #103 #122     ori  $t5, $t0, 13     xori
  //   $t6, $t0, 14     addiu $s5, $s5, 1                #49  #68 #87 #106 #125     bne  $s5, $s6, bistwise
  //   #50 #69 #88 #107 #126     nop     jr $ra                          #127     nop
  //   RS
  //   RT
  //   RD
  //   contents of rom_1 (hex, n*v repeats v):
  //   90 0 1 91 902 a02 0 0 0 150 550 550 250 350 450 20*0 b78 7*0 c44
  //   Immediate
endmodule

module Sign_Extend (
  input  [31:0] in_1,
  output [31:0] out_2
);


  assign out_2 = {{17{in_1[15]}}, in_1[14:0]};
endmodule

module DeandExe (
  input  [5:0] Opcode,
  input  [31:0] A,
  input  [31:0] B,
  input  [4:0] RW,
  input  [31:0] Imediate,
  input  ALU_Src,
  input  CLK,
  output [5:0] out_8,
  output [31:0] Out_A,
  output [31:0] Out_B,
  output [4:0] Out_RW,
  output [31:0] Out_Imediate,
  output Out_ALU_Src
);

  Register #(.width(32)) register_1 (.D(Imediate), .clk(CLK), .Q(Out_Imediate));  // open: en, clr
  Register #(.width(1)) register_2 (.D(ALU_Src), .clk(CLK), .Q(Out_ALU_Src));  // open: en, clr
  Register #(.width(6)) register_3 (.D(Opcode), .clk(CLK), .Q(out_8));  // open: en, clr
  Register #(.width(32)) register_4 (.D(A), .clk(CLK), .Q(Out_A));  // open: en, clr
  Register #(.width(32)) register_5 (.D(B), .clk(CLK), .Q(Out_B));  // open: en, clr
  Register #(.width(5)) register_6 (.D(RW), .clk(CLK), .Q(Out_RW));  // open: en, clr
endmodule

module IFandDe (
  input  [31:0] PC4,
  input  [31:0] Instruction,
  input  CLK,
  output [31:0] Out_PC4,
  output [31:0] Out_Instruction
);

  Register #(.width(32)) register_1 (.D(PC4), .clk(CLK), .Q(Out_PC4));  // open: en, clr
  Register #(.width(32)) register_2 (.D(Instruction), .clk(CLK), .Q(Out_Instruction));  // open: en, clr
endmodule

module Memory (
  input  [31:0] address,
  input  [31:0] Data,
  input  Store,
  input  CLK,
  input  Load,
  input  BW,
  output [31:0] out_7
);

  wire [3:0] dmux_1_out_2, multiplexer_1_out;
  wire [4:3] bit_extender_1_out;
  wire [25:2] bit_extender_1_out_2;
  wire [31:0] shifter_1_out;

  Shifter #(.width(32)) shifter_1 (.in(Data), .\dist ({bit_extender_1_out, 3'b000}), .out(shifter_1_out));
  Bit_Extender #(.in_width(32), .out_width(26)) bit_extender_1 (
    .in(address), .out({bit_extender_1_out_2, bit_extender_1_out}));
  DMUX dmux_1 (.in_1(bit_extender_1_out), .out_2(dmux_1_out_2));
  Multiplexer #(.width(4), .enable("false")) multiplexer_1 (
    .in0(4'b1111), .in1(dmux_1_out_2), .out(multiplexer_1_out), .sel(BW));
  // MIPS_RAM #(.addrWidth(24)) mips_ram_1: pin names not known; wires that end beside it: bit_extender_1_out_2, shifter_1_out, Store, multiplexer_1_out, CLK, Load, out_7
endmodule

module DMUX (
  input  [1:0] in_1,
  output [3:0] out_2
);

  wire not_1_out, not_2_out, not_3_out, not_4_out;

  and and_1 (out_2[3], in_1[0], in_1[1]);
  not not_1 (not_1_out, in_1[1]);
  not not_2 (not_2_out, in_1[0]);
  not not_3 (not_3_out, in_1[0]);
  not not_4 (not_4_out, in_1[1]);
  and and_2 (out_2[1], in_1[0], not_1_out);
  and and_3 (out_2[2], not_2_out, in_1[1]);
  and and_4 (out_2[0], not_3_out, not_4_out);
endmodule

module ALUControl (
  input  [3:0] ALUOp,
  input  [5:0] Func,
  input  [5:0] InstructionOp,
  output [3:0] out_4,
  output JRdetect
);

  wire comparator_1_eq, comparator_2_eq, comparator_3_eq, not_1_out;
  wire [3:0] rom_1_data, rom_2_data;

  Comparator #(.width(4)) comparator_1 (.a(4'b0000), .b(ALUOp), .eq(comparator_1_eq));  // open: gt, lt
  not not_1 (not_1_out, comparator_1_eq);
  ROM #(.addrWidth(6), .dataWidth(4)) rom_1 (.addr(Func), .data(rom_1_data));
  Comparator #(.width(6)) comparator_2 (.a(InstructionOp), .b({6{1'b0}}), .eq(comparator_2_eq));  // open: gt, lt
  Comparator #(.width(6)) comparator_3 (.a(Func), .b(6'b001000), .eq(comparator_3_eq));  // open: gt, lt
  Multiplexer #(.width(4), .enable("false")) multiplexer_1 (
    .in0(rom_1_data), .in1(rom_2_data), .out(out_4), .sel(not_1_out));
  and and_1 (JRdetect, comparator_2_eq, comparator_3_eq);
  ROM #(.addrWidth(4), .dataWidth(4)) rom_2 (.addr(ALUOp), .data(rom_2_data));

  // Notes on the sheet:
  //   contents of rom_1 (hex, n*v repeats v):
  //   0 0 4 5 28*0 2 2 6 6 8 a c e 0 0 f d
  //   contents of rom_2 (hex, n*v repeats v):
  //   0 2 8 a c d 0 0 0 b 9 2 2
endmodule

module ALUUnsign (
  input  [31:0] A,
  input  [31:0] B,
  input  [31:0] Imediate,
  input  [5:0] Func,
  input  [5:0] Opcode,
  output [31:0] out_6
);

  wire comparator_1_eq, comparator_2_lt, comparator_3_lt, multiplexer_2_out, multiplexer_3_out, not_1_out,
       not_2_out;
  wire [31:0] multiplexer_1_out;

  Multiplexer #(.width(32), .enable("false")) multiplexer_1 (
    .in0(B), .in1(Imediate), .out(multiplexer_1_out), .sel(not_1_out));
  not not_1 (not_1_out, comparator_1_eq);
  Comparator #(.width(6)) comparator_1 (.a({6{1'b0}}), .b(Opcode), .eq(comparator_1_eq));  // open: gt, lt
  Comparator #(.width(32)) comparator_2 (.a(A), .b(multiplexer_1_out), .lt(comparator_2_lt));  // open: gt, eq
  Comparator #(.width(32), .mode("unsigned")) comparator_3 (
    .a(A), .b(multiplexer_1_out), .lt(comparator_3_lt));  // open: gt, eq
  Multiplexer #(.enable("false")) multiplexer_2 (
    .in0(comparator_2_lt), .in1(comparator_3_lt), .out(multiplexer_2_out), .sel(multiplexer_3_out));
  Multiplexer #(.enable("false")) multiplexer_3 (
    .in0(Func[0]), .in1(Opcode[0]), .out(multiplexer_3_out), .sel(not_2_out));
  not not_2 (not_2_out, comparator_1_eq);
  assign out_6 = {{31{1'b0}}, multiplexer_2_out};  // Bit_Extender bit_extender_1
endmodule

module DeandExe2 (
  input  [3:0] ALU_Op,
  input  [4:0] Chem,
  input  [5:0] Func,
  input  CLK,
  output [3:0] out_5,
  output [4:0] out_6,
  output [5:0] out_7
);

  Register #(.width(4)) register_1 (.D(ALU_Op), .clk(CLK), .Q(out_5));  // open: en, clr
  Register #(.width(5)) register_2 (.D(Chem), .clk(CLK), .Q(out_6));  // open: en, clr
  Register #(.width(6)) register_3 (.D(Func), .clk(CLK), .Q(out_7));  // open: en, clr
endmodule

module DeandExe3 (
  input  a0,
  input  a1,
  input  a2,
  input  a3,
  input  a4,
  input  a5,
  input  [31:0] PC4,
  input  CLK,
  output out_9,
  output out_10,
  output out_11,
  output out_12,
  output out_13,
  output out_14,
  output [31:0] out_15
);

  Register #(.width(1)) register_1 (.D(a0), .clk(CLK), .Q(out_9));  // open: en, clr
  Register #(.width(1)) register_2 (.D(a1), .clk(CLK), .Q(out_10));  // open: en, clr
  Register #(.width(1)) register_3 (.D(a2), .clk(CLK), .Q(out_11));  // open: en, clr
  Register #(.width(1)) register_4 (.D(a3), .clk(CLK), .Q(out_12));  // open: en, clr
  Register #(.width(1)) register_5 (.D(a4), .clk(CLK), .Q(out_13));  // open: en, clr
  Register #(.width(1)) register_6 (.D(a5), .clk(CLK), .Q(out_14));  // open: en, clr
  Register #(.width(32)) register_7 (.D(PC4), .clk(CLK), .Q(out_15));  // open: en, clr
endmodule

module ExandMem (
  input  a0,
  input  a2,
  input  a3,
  input  a5,
  input  [31:0] A,
  input  [31:0] Result,
  input  [31:0] B,
  input  a4,
  input  [31:0] PC4,
  input  [4:0] rw,
  input  CLK,
  output out_12,
  output out_13,
  output out_14,
  output out_15,
  output [31:0] out_16,
  output [31:0] out_17,
  output [31:0] out_18,
  output out_19,
  output [31:0] out_20,
  output [4:0] out_21
);

  Register #(.width(1)) register_1 (.D(a0), .clk(CLK), .Q(out_12));  // open: en, clr
  Register #(.width(1)) register_2 (.D(a2), .clk(CLK), .Q(out_13));  // open: en, clr
  Register #(.width(1)) register_3 (.D(a3), .clk(CLK), .Q(out_14));  // open: en, clr
  Register #(.width(1)) register_4 (.D(a5), .clk(CLK), .Q(out_15));  // open: en, clr
  Register #(.width(32)) register_5 (.D(A), .clk(CLK), .Q(out_16));  // open: en, clr
  Register #(.width(32)) register_6 (.D(Result), .clk(CLK), .Q(out_17));  // open: en, clr
  Register #(.width(32)) register_7 (.D(B), .clk(CLK), .Q(out_18));  // open: en, clr
  Register #(.width(32)) register_8 (.D(PC4), .clk(CLK), .Q(out_20));  // open: en, clr
  Register #(.width(5)) register_9 (.D(rw), .clk(CLK), .Q(out_21));  // open: en, clr
  Register #(.width(1)) register_10 (.D(a4), .clk(CLK), .Q(out_19));  // open: en, clr
endmodule

module MemandWb (
  input  a0,
  input  a4,
  input  a5,
  input  [31:0] A,
  input  [31:0] Result,
  input  [31:0] PC4,
  input  [4:0] RW,
  input  CLK,
  output out_9,
  output out_10,
  output out_11,
  output [31:0] out_12,
  output [31:0] out_13,
  output [31:0] out_14,
  output [4:0] out_15
);

  Register #(.width(1)) register_1 (.D(a0), .clk(CLK), .Q(out_9));  // open: en, clr
  Register #(.width(1)) register_2 (.D(a5), .clk(CLK), .Q(out_11));  // open: en, clr
  Register #(.width(32)) register_3 (.D(A), .clk(CLK), .Q(out_12));  // open: en, clr
  Register #(.width(32)) register_4 (.D(PC4), .clk(CLK), .Q(out_14));  // open: en, clr
  Register #(.width(5)) register_5 (.D(RW), .clk(CLK), .Q(out_15));  // open: en, clr
  Register #(.width(1)) register_6 (.D(a4), .clk(CLK), .Q(out_10));  // open: en, clr
  Register #(.width(32)) register_7 (.D(Result), .clk(CLK), .Q(out_13));  // open: en, clr
endmodule
