// Logisim project mips_pipeline.circ as structural Verilog
// ALU
module main (
  input  in_1
);

  wire alucontrol_1_jrdetect, and_1_out, CLK, comparator_1_eq, comparator_2_eq, comparator_3_eq,
       comparator_4_eq, comparator_5_eq, comparator_6_eq, comparator_7_eq, comparator_8_eq, comparator_9_eq,
       controlLoadUse, deandex5_1_out_5, deandexe3_1_out_9, deandexe3_1_out_10, deandexe3_1_out_11,
       deandexe3_1_out_12, deandexe3_1_out_13, deandexe3_1_out_14, deandexe_1_out_alu_src, exandmem_1_out_12,
       exandmem_1_out_13, exandmem_1_out_14, exandmem_1_out_15, exandmem_1_out_19, memandwb_1_out_9,
       memandwb_1_out_11, mips_alu_1_p1, multiplexer_10_out, multiplexer_11_out, not_1_out, registerfile_1_p3;
  wire [1:0] forwarding_1_forwordextomem, forwarding_2_forwordextomem;
  wire [3:0] alucontrol_1_out_4, deandexe2_1_out_5, multiplexer_5_out;
  wire [4:0] deandexe2_1_out_6, deandexe4_1_out_4, deandexe_1_out_rw, exandmem_1_out_21, idtoex_rs,
       idtoex_rt, multiplexer_7_out, multiplexer_8_out, multiplexer_9_out, registerfile_1_p4, rt;
  wire [5:0] deandexe2_1_out_7, deandexe_1_out_8, ifandde_1_out_instruction_2;
  wire [11:0] rom_1_data;
  wire [25:0] deandex5_1_out_4, ifandde_1_out_instruction;
  wire [29:0] incrementer_1_p3;
  wire [31:0] adder_1_out, aluunsign_1_out_6, bit_extender_1_out, deandexe3_1_out_15, deandexe_1_out_a,
       deandexe_1_out_b, deandexe_1_out_imediate, exandmem_1_out_16, exandmem_1_out_17, exandmem_1_out_18,
       exandmem_1_out_20, ifandde_1_out_pc4, memandwb_1_out_12, memandwb_1_out_13, memandwb_1_out_14,
       memory_1_out_7, mips_alu_1_p8, mipsprogramrom_1_p2, multiplexer_1_out, multiplexer_2_out,
       multiplexer_3_out, multiplexer_4_out, multiplexer_12_out, multiplexer_13_out, multiplexer_14_out,
       multiplexer_15_out, multiplexer_16_out, register_1_q, registerfile_1_p1, registerfile_1_p7,
       registerfile_1_p8, shifter_1_out, shifter_2_out, sign_extend_1_out_2;

  Multiplexer #(.width(32), .enable("false")) multiplexer_1 (
    .in0(multiplexer_2_out), .in1(deandexe_1_out_a), .out(multiplexer_1_out), .sel(deandex5_1_out_5));
  Multiplexer #(.width(32), .enable("false")) multiplexer_2 (
    .in0(multiplexer_4_out), .in1(shifter_1_out), .out(multiplexer_2_out), .sel(deandexe3_1_out_9));
  // Probe on and_1_out
  Multiplexer #(.width(32), .enable("false")) multiplexer_3 (
    .in0(multiplexer_1_out), .in1(register_1_q), .out(multiplexer_3_out), .sel(controlLoadUse));
  // Probe on and_1_out
  Multiplexer #(.width(32), .enable("false")) multiplexer_4 (
    .in0({incrementer_1_p3, 2'b00}), .in1(adder_1_out), .out(multiplexer_4_out), .sel(and_1_out));
  Register #(.width(32), .trigger("falling")) register_1 (
    .D(multiplexer_3_out), .clk(CLK), .Q(register_1_q), .clr(in_1));  // open: en
  // Probe on adder_1_out
  // Incrementer #(.width(30)) incrementer_1: pin names not known; wires that end beside it: register_1_q[31:2], CLK, incrementer_1_p3
  // MIPSProgramROM mipsprogramrom_1: pin names not known; wires that end beside it: register_1_q, mipsprogramrom_1_p2
  Clock clock_1 (.out(CLK));
  assign bit_extender_1_out = {{6{deandex5_1_out_4[25]}}, deandex5_1_out_4};  // Bit_Extender bit_extender_1
  // Probe on {ifandde_1_out_instruction_2, ifandde_1_out_instruction[25:21], idtoex_rt, ifandde_1_out_instruction[15:0]}
  Shifter #(.width(32)) shifter_1 (.in(bit_extender_1_out), .\dist (5'b00010), .out(shifter_1_out));
  IFandDe ifandde_1 (
    .PC4({incrementer_1_p3, 2'b00}), .Instruction(mipsprogramrom_1_p2), .CLK(CLK),
    .Out_PC4(ifandde_1_out_pc4),
    .Out_Instruction({ifandde_1_out_instruction_2, ifandde_1_out_instruction[25:21], idtoex_rt, ifandde_1_out_instruction[15:0]}));
  ROM #(.addrWidth(6), .dataWidth(12)) rom_1 (.addr(ifandde_1_out_instruction_2), .data(rom_1_data));
  Sign_Extend sign_extend_1 (
    .in_1({ifandde_1_out_instruction_2, ifandde_1_out_instruction[25:21], idtoex_rt, ifandde_1_out_instruction[15:0]}),
    .out_2(sign_extend_1_out_2));
  Multiplexer #(.width(4), .enable("false")) multiplexer_5 (
    .in0(rom_1_data[11:8]), .in1(4'b0000), .out(multiplexer_5_out), .sel(controlLoadUse));
  Multiplexer #(.width(5), .enable("false")) multiplexer_6 (
    .in0(ifandde_1_out_instruction[25:21]), .in1({5{1'b1}}), .out(idtoex_rs), .sel(alucontrol_1_jrdetect));
  Multiplexer #(.width(5), .enable("false")) multiplexer_7 (
    .in0(idtoex_rt), .in1(ifandde_1_out_instruction[15:11]), .out(multiplexer_7_out), .sel(rom_1_data[7]));
  Multiplexer #(.width(5), .enable("false")) multiplexer_8 (
    .in0(multiplexer_7_out), .in1({5{1'b1}}), .out(multiplexer_8_out), .sel(rom_1_data[0]));
  // Probe on rt
  // Probe on idtoex_rt
  // Probe on idtoex_rs
  // RegisterFile #(.trigger("falling")) registerfile_1: pin names not known; wires that end beside it: registerfile_1_p1, CLK, registerfile_1_p3, registerfile_1_p4, idtoex_rs, idtoex_rt, registerfile_1_p7, registerfile_1_p8
  ALUControl alucontrol_1 (
    .ALUOp(multiplexer_5_out), .Func(ifandde_1_out_instruction[5:0]),
    .InstructionOp(ifandde_1_out_instruction_2), .out_4(alucontrol_1_out_4), .JRdetect(alucontrol_1_jrdetect));
  LoadtoUseDetect loadtousedetect_1 (
    .IDtoEXMemRead(deandexe3_1_out_12), .IDtoEXrt(rt), .IFtoIDrs(idtoex_rs), .IFtoIDrt(idtoex_rt),
    .ToControl(controlLoadUse));
  Multiplexer #(.width(5), .enable("false")) multiplexer_9 (
    .in0(multiplexer_8_out), .in1({5{1'b0}}), .out(multiplexer_9_out), .sel(controlLoadUse));
  DeandExe4 deandexe4_1 (.RS(idtoex_rs), .RT(idtoex_rt), .CLK(CLK), .out_4(deandexe4_1_out_4), .out_5(rt));
  DeandEx5 deandex5_1 (
    .Jump({ifandde_1_out_instruction[25:21], idtoex_rt, ifandde_1_out_instruction[15:0]}),
    .JR(alucontrol_1_jrdetect), .in_3(CLK), .out_4(deandex5_1_out_4), .out_5(deandex5_1_out_5));
  Multiplexer #(.enable("false")) multiplexer_10 (
    .in0(rom_1_data[2]), .in1(1'b0), .out(multiplexer_10_out), .sel(controlLoadUse));
  Multiplexer #(.enable("false")) multiplexer_11 (
    .in0(rom_1_data[4]), .in1(1'b0), .out(multiplexer_11_out), .sel(controlLoadUse));
  DeandExe3 deandexe3_1 (
    .a0(rom_1_data[0]), .a1(rom_1_data[1]), .a2(multiplexer_10_out), .a3(rom_1_data[3]),
    .a4(multiplexer_11_out), .a5(rom_1_data[5]), .PC4(ifandde_1_out_pc4), .CLK(CLK),
    .out_9(deandexe3_1_out_9), .out_10(deandexe3_1_out_10), .out_11(deandexe3_1_out_11),
    .out_12(deandexe3_1_out_12), .out_13(deandexe3_1_out_13), .out_14(deandexe3_1_out_14),
    .out_15(deandexe3_1_out_15));
  DeandExe deandexe_1 (
    .Opcode(ifandde_1_out_instruction_2), .A(registerfile_1_p7), .B(registerfile_1_p8),
    .RW(multiplexer_9_out), .Imediate(sign_extend_1_out_2), .ALU_Src(rom_1_data[6]), .CLK(CLK),
    .out_8(deandexe_1_out_8), .Out_A(deandexe_1_out_a), .Out_B(deandexe_1_out_b), .Out_RW(deandexe_1_out_rw),
    .Out_Imediate(deandexe_1_out_imediate), .Out_ALU_Src(deandexe_1_out_alu_src));
  DeandExe2 deandexe2_1 (
    .ALU_Op(alucontrol_1_out_4), .Chem(ifandde_1_out_instruction[10:6]),
    .Func(ifandde_1_out_instruction[5:0]), .CLK(CLK), .out_5(deandexe2_1_out_5), .out_6(deandexe2_1_out_6),
    .out_7(deandexe2_1_out_7));
  // Probe on deandexe_1_out_a
  Shifter #(.width(32)) shifter_2 (.in(deandexe_1_out_imediate), .\dist (5'b00010), .out(shifter_2_out));
  Multiplexer #(.select(2), .width(32), .enable("false")) multiplexer_12 (
    .in0(deandexe_1_out_a), .in1(exandmem_1_out_17), .in2(registerfile_1_p1), .out(multiplexer_12_out),
    .sel(forwarding_1_forwordextomem));  // open: in3
  Multiplexer #(.select(2), .width(32), .enable("false")) multiplexer_13 (
    .in0(deandexe_1_out_b), .in1(exandmem_1_out_17), .in2(registerfile_1_p1), .out(multiplexer_13_out),
    .sel(forwarding_2_forwordextomem));  // open: in3
  Adder #(.width(32)) adder_1 (.a(deandexe3_1_out_15), .b(shifter_2_out), .out(adder_1_out));  // open: cin, cout
  Multiplexer #(.width(32), .enable("false")) multiplexer_14 (
    .in0(multiplexer_13_out), .in1(deandexe_1_out_imediate), .out(multiplexer_14_out),
    .sel(deandexe_1_out_alu_src));
  and and_1 (and_1_out, mips_alu_1_p8[0], deandexe3_1_out_10);
  ALUUnsign aluunsign_1 (
    .A(multiplexer_12_out), .B(multiplexer_13_out), .Imediate(deandexe_1_out_imediate),
    .Func(deandexe2_1_out_7), .Opcode(deandexe_1_out_8), .out_6(aluunsign_1_out_6));
  // Mips_ALU mips_alu_1: pin names not known; wires that end beside it: mips_alu_1_p1, mips_alu_1_p1, multiplexer_12_out, multiplexer_14_out, deandexe2_1_out_5, deandexe2_1_out_5, deandexe2_1_out_6, mips_alu_1_p8
  not not_1 (not_1_out, comparator_1_eq);
  Comparator #(.width(4)) comparator_1 (.a(4'b1101), .b(deandexe2_1_out_5), .eq(comparator_1_eq));  // open: gt, lt
  Multiplexer #(.width(32), .enable("false")) multiplexer_15 (
    .in0(aluunsign_1_out_6), .in1(mips_alu_1_p8), .out(multiplexer_15_out), .sel(not_1_out));
  // Probe on registerfile_1_p4
  // Probe on deandexe4_1_out_4
  // Probe on exandmem_1_out_21
  // Probe on rt
  ExandMem exandmem_1 (
    .a0(deandexe3_1_out_9), .a2(deandexe3_1_out_11), .a3(deandexe3_1_out_12), .a5(deandexe3_1_out_14),
    .A(multiplexer_15_out), .Result(multiplexer_15_out), .B(multiplexer_13_out), .a4(deandexe3_1_out_13),
    .PC4(deandexe3_1_out_15), .rw(deandexe_1_out_rw), .CLK(CLK), .out_12(exandmem_1_out_12),
    .out_13(exandmem_1_out_13), .out_14(exandmem_1_out_14), .out_15(exandmem_1_out_15),
    .out_16(exandmem_1_out_16), .out_17(exandmem_1_out_17), .out_18(exandmem_1_out_18),
    .out_19(exandmem_1_out_19), .out_20(exandmem_1_out_20), .out_21(exandmem_1_out_21));
  Comparator #(.width(5)) comparator_2 (.a(exandmem_1_out_21), .b({5{1'b0}}), .eq(comparator_2_eq));  // open: gt, lt
  Comparator #(.width(5)) comparator_3 (
    .a(exandmem_1_out_21), .b(deandexe4_1_out_4), .eq(comparator_3_eq));  // open: gt, lt
  Comparator #(.width(5)) comparator_4 (.a(registerfile_1_p4), .b({5{1'b0}}), .eq(comparator_4_eq));  // open: gt, lt
  Comparator #(.width(5)) comparator_5 (
    .a(registerfile_1_p4), .b(deandexe4_1_out_4), .eq(comparator_5_eq));  // open: gt, lt
  Comparator #(.width(5)) comparator_6 (.a(exandmem_1_out_21), .b({5{1'b0}}), .eq(comparator_6_eq));  // open: gt, lt
  Comparator #(.width(5)) comparator_7 (.a(exandmem_1_out_21), .b(rt), .eq(comparator_7_eq));  // open: gt, lt
  Comparator #(.width(5)) comparator_8 (.a(registerfile_1_p4), .b({5{1'b0}}), .eq(comparator_8_eq));  // open: gt, lt
  Comparator #(.width(5)) comparator_9 (.a(registerfile_1_p4), .b(rt), .eq(comparator_9_eq));  // open: gt, lt
  Memory memory_1 (
    .address(exandmem_1_out_17), .Data(exandmem_1_out_18), .Store(exandmem_1_out_13), .CLK(CLK),
    .Load(exandmem_1_out_14), .BW(1'b0), .out_7(memory_1_out_7));
  // Probe on forwarding_1_forwordextomem
  Forwarding forwarding_1 (
    .MemtoWbequal(comparator_5_eq), .ExtoMemequal(comparator_3_eq), .MemtoWbZero(comparator_4_eq),
    .EXtoMEMzero(comparator_2_eq), .RegWritefromEXtoMem(exandmem_1_out_19),
    .RegWritefromMEMtoWB(registerfile_1_p3), .forwordEXtoMEM(forwarding_1_forwordextomem[0]),
    .forwardMEMtoWB(forwarding_1_forwordextomem[1]));
  Forwarding forwarding_2 (
    .MemtoWbequal(comparator_9_eq), .ExtoMemequal(comparator_7_eq), .MemtoWbZero(comparator_8_eq),
    .EXtoMEMzero(comparator_6_eq), .RegWritefromEXtoMem(exandmem_1_out_19),
    .RegWritefromMEMtoWB(registerfile_1_p3), .forwordEXtoMEM(forwarding_2_forwordextomem[0]),
    .forwardMEMtoWB(forwarding_2_forwordextomem[1]));
  // Probe on forwarding_2_forwordextomem
  // Probe on registerfile_1_p4
  MemandWb memandwb_1 (
    .a0(exandmem_1_out_12), .a4(exandmem_1_out_19), .a5(exandmem_1_out_15), .A(exandmem_1_out_16),
    .Result(memory_1_out_7), .PC4(exandmem_1_out_20), .RW(exandmem_1_out_21), .CLK(CLK),
    .out_9(memandwb_1_out_9), .out_10(registerfile_1_p3), .out_11(memandwb_1_out_11),
    .out_12(memandwb_1_out_12), .out_13(memandwb_1_out_13), .out_14(memandwb_1_out_14),
    .out_15(registerfile_1_p4));
  // Probe on registerfile_1_p1
  Multiplexer #(.width(32), .enable("false")) multiplexer_16 (
    .in0(memandwb_1_out_12), .in1(memandwb_1_out_13), .out(multiplexer_16_out), .sel(memandwb_1_out_11));
  Multiplexer #(.width(32), .enable("false")) multiplexer_17 (
    .in0(multiplexer_16_out), .in1(memandwb_1_out_14), .out(registerfile_1_p1), .sel(memandwb_1_out_9));

  // Notes on the sheet:
  //   contents of mipsprogramrom_1 (hex, n*v repeats v):
  //   addu $s1, $zero, $zero                  # 5     addu $s3, $zero, $zero                  # 6
  //   addiu $sp, $sp, -4                              # 7     addiu $s0, $0, 5
  //   # 8     sw $s0, 0($sp)                                  # 9     jal HAILSTONE
  //   # 10    nop                                                             # 11    addiu $sp, $sp, 4
  //   # 74    addu $s1, $s1, $v0                              # 75    addiu $sp, $sp, -12
  //   # 76    sw $s1, 8($sp)                                  # 77    addiu $s1, $s1, 1
  //   # 78    sw $s1, 4($sp)                                  # 79    addiu $s1, $s1, 1
  //   # 80    sw $s1, 0($sp)                                  # 81    lw $s2, 8($sp)
  //   # 82    addu $s3, $s2, $zero                    # 84    lw $s2, 4($sp)
  //   # 85        addu $s3, $s2, $s3              # 87    lw $s2, 0($sp)
  //   # 88    addu $s3, $s2, $s3                  # 90        nop
  //   # 91    nop                                                             # 92    nop
  //   # 93    nop                                                             # 94    nop
  //   # 95  HAILSTONE:        addiu $sp, $sp, -8                              # 12    sw $ra, 4($sp)
  //   # 13    sw $fp, 0($sp)                                  # 14    addu $fp, $sp, $zero
  //   # 15    lw $t0, 8($fp)                                  # 16    addiu $t1, $zero, 1
  //   # 17    addu $t2, $zero, $zero          # 18 WHILE:     beq $t0, $t1, WHILE_OUT         # 19  30  39
  //   48  57  66        nop # delayed slot                              # 20  31  40  49  58  67 WHILE_IN:
  //   addiu $t2, $t2, 1               # 21  32  41  50  59    andi $t3, $t0, 1
  //   # 22  33  42  51  60    bne $t3, $zero, ELSE                    # 23  34  43  52  61    nop #
  //   delayed slot              # 24  35  44  53  62 IF:        sra $t0, $t0, 1                         #
  //   36  45  54  63    j WHILE                                                 #         37  46  55  64
  //   nop                                                             #         38  47  56  65 ELSE:  addu
  //   $t4, $t0, $t0              # 25    addu $t0, $t0, $t4              # 26    addiu $t0, $t0, 1
  //   # 27    j WHILE                                                 # 28    nop
  //   # 29 WHILE_OUT:         lw $ra, 4($sp)                              # 68        lw $fp, 0($sp)
  //   # 69    addiu $sp, $sp, 8                               # 70    addu $v0, $t2, $zero
  //   # 71    jr $ra                                                  # 72    nop
  //   # 73
  //   RS
  //   RT
  //   RD
  //   contents of rom_1 (hex, n*v repeats v):
  //   90 0 1 91 902 a02 0 0 0 150 550 550 250 350 450 20*0 b78 7*0 c44
  //   Immediate
  //   RS
  //   RW EXtoME
  //   RT
  //   RW of MEtoWB
  //   ALU Result
  //   ALU Result
endmodule

module Sign_Extend (
  input  [31:0] in_1,
  output [31:0] out_2
);


  assign out_2 = {{17{in_1[15]}}, in_1[14:0]};
endmodule

module DeandExe (
  input  [5:0] Opcode,
  input  [31:0] A,
  input  [31:0] B,
  input  [4:0] RW,
  input  [31:0] Imediate,
  input  ALU_Src,
  input  CLK,
  output [5:0] out_8,
  output [31:0] Out_A,
  output [31:0] Out_B,
  output [4:0] Out_RW,
  output [31:0] Out_Imediate,
  output Out_ALU_Src
);

  Register #(.width(32)) register_1 (.D(Imediate), .clk(CLK), .Q(Out_Imediate));  // open: en, clr
  Register #(.width(1)) register_2 (.D(ALU_Src), .clk(CLK), .Q(Out_ALU_Src));  // open: en, clr
  Register #(.width(6)) register_3 (.D(Opcode), .clk(CLK), .Q(out_8));  // open: en, clr
  Register #(.width(32)) register_4 (.D(A), .clk(CLK), .Q(Out_A));  // open: en, clr
  Register #(.width(32)) register_5 (.D(B), .clk(CLK), .Q(Out_B));  // open: en, clr
  Register #(.width(5)) register_6 (.D(RW), .clk(CLK), .Q(Out_RW));  // open: en, clr
endmodule

module IFandDe (
  input  [31:0] PC4,
  input  [31:0] Instruction,
  input  CLK,
  output [31:0] Out_PC4,
  output [31:0] Out_Instruction
);

  Register #(.width(32)) register_1 (.D(PC4), .clk(CLK), .Q(Out_PC4));  // open: en, clr
  Register #(.width(32)) register_2 (.D(Instruction), .clk(CLK), .Q(Out_Instruction));  // open: en, clr
endmodule

module Memory (
  input  [31:0] address,
  input  [31:0] Data,
  input  Store,
  input  CLK,
  input  Load,
  input  BW,
  output [31:0] out_7
);

  wire [3:0] dmux_1_out_2, multiplexer_1_out;
  wire [4:3] bit_extender_1_out;
  wire [25:2] bit_extender_1_out_2;
  wire [31:0] shifter_1_out;

  Shifter #(.width(32)) shifter_1 (.in(Data), .\dist ({bit_extender_1_out, 3'b000}), .out(shifter_1_out));
  Bit_Extender #(.in_width(32), .out_width(26)) bit_extender_1 (
    .in(address), .out({bit_extender_1_out_2, bit_extender_1_out}));
  DMUX dmux_1 (.in_1(bit_extender_1_out), .out_2(dmux_1_out_2));
  Multiplexer #(.width(4), .enable("false")) multiplexer_1 (
    .in0(4'b1111), .in1(dmux_1_out_2), .out(multiplexer_1_out), .sel(BW));
  // MIPS_RAM #(.addrWidth(24)) mips_ram_1: pin names not known; wires that end beside it: bit_extender_1_out_2, shifter_1_out, Store, multiplexer_1_out, CLK, Load, out_7
endmodule

module DMUX (
  input  [1:0] in_1,
  output [3:0] out_2
);

  wire not_1_out, not_2_out, not_3_out, not_4_out;

  and and_1 (out_2[3], in_1[0], in_1[1]);
  not not_1 (not_1_out, in_1[1]);
  not not_2 (not_2_out, in_1[0]);
  not not_3 (not_3_out, in_1[0]);
  not not_4 (not_4_out, in_1[1]);
  and and_2 (out_2[1], in_1[0], not_1_out);
  and and_3 (out_2[2], not_2_out, in_1[1]);
  and and_4 (out_2[0], not_3_out, not_4_out);
endmodule

module ALUControl (
  input  [3:0] ALUOp,
  input  [5:0] Func,
  input  [5:0] InstructionOp,
  output [3:0] out_4,
  output JRdetect
);

  wire comparator_1_eq, comparator_2_eq, comparator_3_eq, not_1_out;
  wire [3:0] rom_1_data, rom_2_data;

  Comparator #(.width(4)) comparator_1 (.a(4'b0000), .b(ALUOp), .eq(comparator_1_eq));  // open: gt, lt
  not not_1 (not_1_out, comparator_1_eq);
  ROM #(.addrWidth(6), .dataWidth(4)) rom_1 (.addr(Func), .data(rom_1_data));
  Comparator #(.width(6)) comparator_2 (.a(InstructionOp), .b({6{1'b0}}), .eq(comparator_2_eq));  // open: gt, lt
  Comparator #(.width(6)) comparator_3 (.a(Func), .b(6'b001000), .eq(comparator_3_eq));  // open: gt, lt
  Multiplexer #(.width(4), .enable("false")) multiplexer_1 (
    .in0(rom_1_data), .in1(rom_2_data), .out(out_4), .sel(not_1_out));
  and and_1 (JRdetect, comparator_2_eq, comparator_3_eq);
  ROM #(.addrWidth(4), .dataWidth(4)) rom_2 (.addr(ALUOp), .data(rom_2_data));

  // Notes on the sheet:
  //   contents of rom_1 (hex, n*v repeats v):
  //   0 0 4 5 28*0 2 2 6 6 8 a c e 0 0 f d
  //   contents of rom_2 (hex, n*v repeats v):
  //   0 2 8 a c d 0 0 0 b 9 2 2
endmodule

module ALUUnsign (
  input  [31:0] A,
  input  [31:0] B,
  input  [31:0] Imediate,
  input  [5:0] Func,
  input  [5:0] Opcode,
  output [31:0] out_6
);

  wire comparator_1_eq, comparator_2_lt, comparator_3_lt, multiplexer_2_out, multiplexer_3_out, not_1_out,
       not_2_out;
  wire [31:0] multiplexer_1_out;

  Multiplexer #(.width(32), .enable("false")) multiplexer_1 (
    .in0(B), .in1(Imediate), .out(multiplexer_1_out), .sel(not_1_out));
  not not_1 (not_1_out, comparator_1_eq);
  Comparator #(.width(6)) comparator_1 (.a({6{1'b0}}), .b(Opcode), .eq(comparator_1_eq));  // open: gt, lt
  Comparator #(.width(32)) comparator_2 (.a(A), .b(multiplexer_1_out), .lt(comparator_2_lt));  // open: gt, eq
  Comparator #(.width(32), .mode("unsigned")) comparator_3 (
    .a(A), .b(multiplexer_1_out), .lt(comparator_3_lt));  // open: gt, eq
  Multiplexer #(.enable("false")) multiplexer_2 (
    .in0(comparator_2_lt), .in1(comparator_3_lt), .out(multiplexer_2_out), .sel(multiplexer_3_out));
  Multiplexer #(.enable("false")) multiplexer_3 (
    .in0(Func[0]), .in1(Opcode[0]), .out(multiplexer_3_out), .sel(not_2_out));
  not not_2 (not_2_out, comparator_1_eq);
  assign out_6 = {{31{1'b0}}, multiplexer_2_out};  // Bit_Extender bit_extender_1
endmodule

module DeandExe2 (
  input  [3:0] ALU_Op,
  input  [4:0] Chem,
  input  [5:0] Func,
  input  CLK,
  output [3:0] out_5,
  output [4:0] out_6,
  output [5:0] out_7
);

  Register #(.width(4)) register_1 (.D(ALU_Op), .clk(CLK), .Q(out_5));  // open: en, clr
  Register #(.width(5)) register_2 (.D(Chem), .clk(CLK), .Q(out_6));  // open: en, clr
  Register #(.width(6)) register_3 (.D(Func), .clk(CLK), .Q(out_7));  // open: en, clr
endmodule

module DeandExe3 (
  input  a0,
  input  a1,
  input  a2,
  input  a3,
  input  a4,
  input  a5,
  input  [31:0] PC4,
  input  CLK,
  output out_9,
  output out_10,
  output out_11,
  output out_12,
  output out_13,
  output out_14,
  output [31:0] out_15
);

  Register #(.width(1)) register_1 (.D(a0), .clk(CLK), .Q(out_9));  // open: en, clr
  Register #(.width(1)) register_2 (.D(a1), .clk(CLK), .Q(out_10));  // open: en, clr
  Register #(.width(1)) register_3 (.D(a2), .clk(CLK), .Q(out_11));  // open: en, clr
  Register #(.width(1)) register_4 (.D(a3), .clk(CLK), .Q(out_12));  // open: en, clr
  Register #(.width(1)) register_5 (.D(a4), .clk(CLK), .Q(out_13));  // open: en, clr
  Register #(.width(1)) register_6 (.D(a5), .clk(CLK), .Q(out_14));  // open: en, clr
  Register #(.width(32)) register_7 (.D(PC4), .clk(CLK), .Q(out_15));  // open: en, clr
endmodule

module ExandMem (
  input  a0,
  input  a2,
  input  a3,
  input  a5,
  input  [31:0] A,
  input  [31:0] Result,
  input  [31:0] B,
  input  a4,
  input  [31:0] PC4,
  input  [4:0] rw,
  input  CLK,
  output out_12,
  output out_13,
  output out_14,
  output out_15,
  output [31:0] out_16,
  output [31:0] out_17,
  output [31:0] out_18,
  output out_19,
  output [31:0] out_20,
  output [4:0] out_21
);

  Register #(.width(1)) register_1 (.D(a0), .clk(CLK), .Q(out_12));  // open: en, clr
  Register #(.width(1)) register_2 (.D(a2), .clk(CLK), .Q(out_13));  // open: en, clr
  Register #(.width(1)) register_3 (.D(a3), .clk(CLK), .Q(out_14));  // open: en, clr
  Register #(.width(1)) register_4 (.D(a5), .clk(CLK), .Q(out_15));  // open: en, clr
  Register #(.width(32)) register_5 (.D(A), .clk(CLK), .Q(out_16));  // open: en, clr
  Register #(.width(32)) register_6 (.D(Result), .clk(CLK), .Q(out_17));  // open: en, clr
  Register #(.width(32)) register_7 (.D(B), .clk(CLK), .Q(out_18));  // open: en, clr
  Register #(.width(32)) register_8 (.D(PC4), .clk(CLK), .Q(out_20));  // open: en, clr
  Register #(.width(5)) register_9 (.D(rw), .clk(CLK), .Q(out_21));  // open: en, clr
  Register #(.width(1)) register_10 (.D(a4), .clk(CLK), .Q(out_19));  // open: en, clr
endmodule

module MemandWb (
  input  a0,
  input  a4,
  input  a5,
  input  [31:0] A,
  input  [31:0] Result,
  input  [31:0] PC4,
  input  [4:0] RW,
  input  CLK,
  output out_9,
  output out_10,
  output out_11,
  output [31:0] out_12,
  output [31:0] out_13,
  output [31:0] out_14,
  output [4:0] out_15
);

  Register #(.width(1)) register_1 (.D(a0), .clk(CLK), .Q(out_9));  // open: en, clr
  Register #(.width(1)) register_2 (.D(a5), .clk(CLK), .Q(out_11));  // open: en, clr
  Register #(.width(32)) register_3 (.D(A), .clk(CLK), .Q(out_12));  // open: en, clr
  Register #(.width(32)) register_4 (.D(PC4), .clk(CLK), .Q(out_14));  // open: en, clr
  Register #(.width(5)) register_5 (.D(RW), .clk(CLK), .Q(out_15));  // open: en, clr
  Register #(.width(1)) register_6 (.D(a4), .clk(CLK), .Q(out_10));  // open: en, clr
  Register #(.width(32)) register_7 (.D(Result), .clk(CLK), .Q(out_13));  // open: en, clr
endmodule

module Forwarding (
  input  MemtoWbequal,
  input  ExtoMemequal,
  input  MemtoWbZero,
  input  EXtoMEMzero,
  input  RegWritefromEXtoMem,
  input  RegWritefromMEMtoWB,
  output forwordEXtoMEM,
  output forwardMEMtoWB
);

  wire and_1_out, and_2_out, and_3_out, and_4_out, not_1_out, not_2_out, not_3_out, not_4_out, not_5_out,
       not_6_out, not_7_out, not_8_out, not_9_out;

  not not_1 (not_1_out, MemtoWbequal);
  not not_2 (not_2_out, EXtoMEMzero);
  not not_3 (not_3_out, MemtoWbZero);
  not not_4 (not_4_out, EXtoMEMzero);
  not not_5 (not_5_out, ExtoMemequal);
  not not_6 (not_6_out, MemtoWbZero);
  not not_7 (not_7_out, MemtoWbZero);
  not not_8 (not_8_out, EXtoMEMzero);
  not not_9 (not_9_out, RegWritefromEXtoMem);
  and and_1 (and_1_out, not_1_out, ExtoMemequal, not_2_out, RegWritefromEXtoMem);
  and and_2 (and_2_out, ExtoMemequal, not_3_out, not_4_out, RegWritefromEXtoMem);
  and and_3 (and_3_out, MemtoWbequal, not_5_out, not_6_out, RegWritefromMEMtoWB);
  and and_4 (and_4_out, MemtoWbequal, not_7_out, not_8_out, not_9_out, RegWritefromMEMtoWB);
  or or_1 (forwordEXtoMEM, and_1_out, and_2_out);
  or or_2 (forwardMEMtoWB, and_3_out, and_4_out);
endmodule

module DeandExe4 (
  input  [4:0] RS,
  input  [4:0] RT,
  input  CLK,
  output [4:0] out_4,
  output [4:0] out_5
);

  Register #(.width(5)) register_1 (.D(RS), .clk(CLK), .Q(out_4));  // open: en, clr
  Register #(.width(5)) register_2 (.D(RT), .clk(CLK), .Q(out_5));  // open: en, clr
endmodule

module LoadtoUseDetect (
  input  IDtoEXMemRead,
  input  [4:0] IDtoEXrt,
  input  [4:0] IFtoIDrs,
  input  [4:0] IFtoIDrt,
  output ToControl
);

  wire comparator_1_eq, comparator_2_eq, or_1_out;

  Comparator #(.width(5)) comparator_1 (.a(IDtoEXrt), .b(IFtoIDrs), .eq(comparator_1_eq));  // open: gt, lt
  Comparator #(.width(5)) comparator_2 (.a(IDtoEXrt), .b(IFtoIDrt), .eq(comparator_2_eq));  // open: gt, lt
  or or_1 (or_1_out, comparator_1_eq, comparator_2_eq);
  and and_1 (ToControl, IDtoEXMemRead, or_1_out);
endmodule

module DeandEx5 (
  input  [25:0] Jump,
  input  JR,
  input  in_3,
  output [25:0] out_4,
  output out_5
);

  Register #(.width(26)) register_1 (.D(Jump), .clk(in_3), .Q(out_4));  // open: en, clr
  Register #(.width(1)) register_2 (.D(JR), .clk(in_3), .Q(out_5));  // open: en, clr
endmodule
